// Logisim project 8-bit TTL Cpu.circ as structural Verilog: 1 circuit, main circuit main
module main (
);

  wire and_1_out, and_2_out, and_3_out, and_4_out, and_5_out, and_6_out, CLK_B, clock_1_out, d_ff_1_q,
       decoder_1_out4, decoder_2_out0, En_Reg_Clk, Execute, Fetch_1, Fetch_2, Fetch_3, nand_1_out, or_1_out,
       PC_Next, Reset;
  wire [2:0] counter_1_q, R1_Addr, R2_Addr;
  wire [5:0] OPCODE;
  wire [7:0] A_q, ram_1_data;
  wire [11:0] adder_1_out, Addr, PC_q;

  Clock clock_1 (.out(clock_1_out));
  and and_1 (and_1_out, nand_1_out, clock_1_out);
  D_Flip_Flop d_ff_1 (.clk(and_1_out), .D(1'b1), .Q(d_ff_1_q), .reset(Reset));  // open: Qn, preset, en
  nand nand_1 (nand_1_out, clock_1_out, d_ff_1_q);
  Counter #(.width(3), .max('h7)) counter_1 (
    .count(1'b1), .Q(counter_1_q), .clk(nand_1_out), .clr(or_1_out));  // open: load, D, carry
  Decoder #(.select(3)) decoder_1 (
    .out0(Fetch_1), .out1(Fetch_2), .out2(Fetch_3), .out3(Execute), .out4(decoder_1_out4), .sel(counter_1_q));  // open: out5, out6, out7, en
  or or_1 (or_1_out, decoder_1_out4, Reset);
  not not_1 (CLK_B, nand_1_out);
  Adder #(.width(12)) adder_1 (.a(PC_q), .b(12'h1), .out(adder_1_out));  // open: cin, cout
  Decoder #(.select(3)) decoder_2 (
    .out0(decoder_2_out0), .sel(R1_Addr));  // open: out1, out2, out3, out4, out5, out6, out7, en
  Register #(.width(12)) PC (.D(adder_1_out), .Q(PC_q), .clk(PC_Next), .clr(Reset));  // open: en
  Button button_1 (.out(Reset));
  and and_2 (and_2_out, CLK_B, Execute, En_Reg_Clk);
  RAM #(.addrWidth(12), .bus("asynch")) ram_1 (.addr(PC_q), .data(ram_1_data), .sel(1'b1), .ld(1'b1));  // open: clr
  and and_3 (and_3_out, decoder_2_out0, and_2_out);
  Register A (.D(Addr[7:0]), .Q(A_q), .clk(and_3_out), .clr(Reset));  // open: en
  and and_4 (and_4_out, Fetch_3, CLK_B);
  and and_5 (and_5_out, Fetch_2, CLK_B);
  and and_6 (and_6_out, Fetch_1, CLK_B);
  Register IR_3 (.D(ram_1_data), .Q(Addr[7:0]), .clk(and_4_out), .clr(Reset));  // open: en
  Register IR_2 (.D(ram_1_data), .Q({R1_Addr[0], R2_Addr, Addr[11:8]}), .clk(and_5_out), .clr(Reset));  // open: en
  Register IR_1 (.D(ram_1_data), .Q({OPCODE, R1_Addr[2:1]}), .clk(and_6_out), .clr(Reset));  // open: en
  or or_2 (PC_Next, and_4_out, and_5_out, and_6_out);

  // Other names for the same wires on the sheet: Data[7:0] = Addr[7:0]

  // Notes on the sheet:
  //   This odd block is just to make sure the initial state on reset will always be Fetch-1 High and CLK-B Low
  //   JACA-2 - 8-bit Homebrew CPU
  //   v. 0.3.0
  //   Equiv to 74HCT4017
  //   RAM
  //   Least significant byte
endmodule
